# Fritzing sketch OttoOnWemosD1 (saved by Fritzing 0.9.3b)
breadboards: 1

parts:
  M2 = Dagu DGServo 9g (Top view) [part_number=RS001B]
  J1 = Piezo Speaker
  WeMos_D1_Mini1 = WeMos D1 Mini  # not connected
  J2 = Dagu DGServo 9g header connector (female) [package=THT]
  M3 = Dagu DGServo 9g (Top view) [part_number=RS001B]
  J3 = Dagu DGServo 9g header connector (female) [package=THT]
  M4 = Dagu DGServo 9g (Top view) [part_number=RS001B]
  J4 = Dagu DGServo 9g header connector (female) [package=THT]
  M5 = Dagu DGServo 9g (Top view) [part_number=RS001B]
  J5 = Dagu DGServo 9g header connector (female) [package=THT]

nets:
  GND: M2.gnd, J1.pin1, J2.pulse, M3.gnd, J3.pulse, M4.gnd, J4.pulse, M5.gnd, J5.pulse
  VCC: M2.vcc, J2.Vcc, M3.vcc, J3.Vcc, M4.vcc, J4.Vcc, M5.vcc, J5.Vcc
  N1: M2.pulse, J2.gnd
  N2: M3.pulse, J3.gnd
  N3: M4.pulse, J4.gnd
  N4: M5.pulse, J5.gnd
